# Fritzing sketch kalitka maketnaya (saved by Fritzing 0.9.3b)

parts:
  KEYPAD1 = Membrane Matrix Keypad
  S1 = Pushbutton [package="[THT]"]
  Часть4 = Arduino Mega 2560 (Rev3)
  J4 = Basic Servo
  L2 = Solenoid
  Module1 = Relay
  VCC2 = 4 x AAA Battery Mount
  J3 = Piezo Speaker
  hc-sr6 = hc-sr04

nets:
  N1: KEYPAD1.1, Часть4.D12_PWM
  N2: KEYPAD1.2, Часть4.D11_PWM
  N3: KEYPAD1.3, Часть4.D10_PWM
  N4: KEYPAD1.4, Часть4.D9_PWM
  N5: KEYPAD1.5, Часть4.D8_PWM
  N6: KEYPAD1.6, Часть4.D7_PWM
  N7: KEYPAD1.7, Часть4.D6_PWM
  GND: S1.Pin_1, S1.Pin_2, Часть4.GND, J4.gnd, Module1.ground, J3.pin1, hc-sr6.GND
  N8: S1.Pin_4, Часть4.D2_PWM
  VCC: Часть4.5V, J4.vcc, Module1.power, hc-sr6.VCC
  N9: Часть4.D3_PWM, J4.pulse
  N10: Часть4.D5_PWM, J3.pin2
  N11: Часть4.D22, Module1.signal
  N12: Часть4.D41, hc-sr6.Echo
  N13: Часть4.D43, hc-sr6.Trig
  N14: L2.pin1, VCC2.-
  N15: L2.pin2, Module1.NC, Module1.C, Module1.NO, VCC2.+

custom parts:
  Membrane Matrix Keypad: Membrane Matrix 3x4 Keypad
