# Fritzing sketch vorota maketnaya (saved by Fritzing 0.9.3b)
breadboards: 1

parts:
  LED1 = RGB LED (com. cathode, rgb) [package="5 mm [THT]"]
  hc-sr1 = hc-sr04
  Часть2 = RFID-RC522-v2
  S1 = Pushbutton [package="[THT]"]
  S2 = Pushbutton [package="[THT]"]
  C2 = Electrolytic Capacitor [capacitance=47µF voltage=20V package="200 mil [THT, electrolytic]"]
  M2 = Stepper Motor - Bipolar
  Power_plug2 = Power plug [part_number="PSU 12V 10A"]
  S3 = Pushbutton [package="[THT]"]
  Часть1 = Arduino Mega 2560 (Rev3)
  OLED_I2C1 = OLED 128x64 I2C Monochrome Display
  Raspberry_Pi_1 = Raspberry Pi 3 [part_number=RPI-3-V1.2]
  Pololu_A1 = Pololu A4988 [package=SO16]

nets (from the schematic view):
  N1: LED1.red_anode, Часть1.D4_PWM
  GND: LED1.common_cathode, hc-sr1.GND, Часть2.RST, S1.Pin_2, S2.Pin_2, S3.Pin_4, Часть1.GND, OLED_I2C1.GND, Raspberry_Pi_1.GND, Pololu_A1.GND#8
  N2: LED1.green_anode, Часть1.D3_PWM
  N3: LED1.blue_anode, Часть1.D2_PWM
  VCC: hc-sr1.VCC, Часть1.IOREF, Pololu_A1.VDD
  N4: hc-sr1.Trig, Часть1.D43
  N5: hc-sr1.Echo, Часть1.D41
  N6: Часть2.SDA, Часть1.D9_PWM
  N7: Часть2.SCK, Часть1.D52
  N8: Часть2.MOSI, Часть1.D51
  N9: Часть2.MISO, Часть1.D50
  N10: Часть2.GND, Часть1.D8_PWM
  3.3V: Часть2.3.3V, Часть1.3V3, OLED_I2C1.VDD
  N11: S1.Pin_3, S1.Pin_4, Часть1.D6_PWM
  N12: S2.Pin_4, Часть1.D7_PWM
  N13: C2.-, Power_plug2.GND, Pololu_A1.GND#14
  N14: C2.+, Power_plug2.VCC, Pololu_A1.VMOT
  N15: M2.A, Pololu_A1.2B
  N16: M2.C, Pololu_A1.2A
  N17: M2.B, Pololu_A1.1A
  N18: M2.D, Pololu_A1.1B
  N19: S3.Pin_1, S3.Pin_2, Часть1.D5_PWM
  N20: Часть1.D21/SCL, OLED_I2C1.SCK
  N21: Часть1.D20/SDA, Часть1.SDA, OLED_I2C1.SDA
  N22: Часть1.D15/RX3, Raspberry_Pi_1.GPIO14
  N23: Часть1.D14/TX3, Raspberry_Pi_1.GPIO15
  N24: Часть1.D11_PWM, Pololu_A1.STEP
  N25: Часть1.D10_PWM, Pololu_A1.DIR
  N26: Pololu_A1.RESET, Pololu_A1.SLEEP

custom parts:
  RFID-RC522-v2: A simple China made RFID-RC522 Reader; do check the pin labels, as this is a MFRC522 based clone.
